# Fritzing sketch whalefallschematic (saved by Fritzing 0.9.3b)
breadboards: 1

parts:
  mcu = Arduino Mega 2560 (Rev3)
  R1 = Resistor [tolerance=±5% resistance=220 package=THT]
  whale1 = HALL-EFFECT [package=sc70]
  R5 = Resistor [tolerance=±5% resistance=220 package="2010 [SMD]"]
  creature1 = LED - 3mm [color="Blue (470nm)" package="3 mm [THT]"]
  Q1 = TRANSISTOR_NPN [package=to-92-ammo]
  R2 = Resistor [tolerance=±5% resistance=220 package=THT]
  whale2 = HALL-EFFECT [package=sc70]
  R3 = Resistor [tolerance=±5% resistance=220 package=THT]
  whale3 = HALL-EFFECT [package=sc70]
  R4 = Resistor [tolerance=±5% resistance=220 package=THT]
  whale4 = HALL-EFFECT [package=sc70]
  R9 = Resistor [tolerance=±5% resistance=10k package="2010 [SMD]"]
  R6 = Resistor [tolerance=±5% resistance=220 package="2010 [SMD]"]
  Q2 = TRANSISTOR_NPN [package=to-92-ammo]
  creature2 = LED - 3mm [color="Blue (470nm)" package="3 mm [THT]"]
  R10 = Resistor [tolerance=±5% resistance=10k package="2010 [SMD]"]
  R11 = Resistor [tolerance=±5% resistance=10k package="2010 [SMD]"]
  R7 = Resistor [tolerance=±5% resistance=220 package="2010 [SMD]"]
  Q3 = TRANSISTOR_NPN [package=to-92-ammo]
  creature3 = LED - 3mm [color="Blue (470nm)" package="3 mm [THT]"]
  R12 = Resistor [tolerance=±5% resistance=10k package="2010 [SMD]"]
  R8 = Resistor [tolerance=±5% resistance=220 package="2010 [SMD]"]
  Q4 = TRANSISTOR_NPN [package=to-92-ammo]
  creature4 = LED - 3mm [color="Blue (470nm)" package="3 mm [THT]"]
  buzzer = Piezo Speaker

nets:
  N1: mcu.A2, R1.Pin_1, whale1.OUT, R9.Pin_0
  N2: mcu.A3, R2.Pin_1, whale2.OUT, R10.Pin_0
  N3: mcu.A4, R3.Pin_1, whale3.OUT, R11.Pin_0
  N4: mcu.A5, R4.Pin_1, whale4.OUT, R12.Pin_0
  GND: mcu.GND, whale1.GND, creature1.cathode, Q1.E, whale2.GND, whale3.GND, whale4.GND, Q2.E, creature2.cathode, Q3.E, creature3.cathode, Q4.E, creature4.cathode, buzzer.pin2
  N5: mcu.IOREF, buzzer.pin1
  VCC: mcu.5V, R1.Pin_0, whale1.VCC, R5.Pin_0, R2.Pin_0, whale2.VCC, R3.Pin_0, whale3.VCC, R4.Pin_0, whale4.VCC, R6.Pin_0, R7.Pin_0, R8.Pin_0
  N6: R5.Pin_1, creature1.anode, Q1.C
  N7: Q1.B, R9.Pin_1
  N8: R6.Pin_1, Q2.C, creature2.anode
  N9: Q2.B, R10.Pin_1
  N10: R11.Pin_1, Q3.B
  N11: R7.Pin_1, Q3.C, creature3.anode
  N12: R12.Pin_1, Q4.B
  N13: R8.Pin_1, Q4.C, creature4.anode
